# Fritzing sketch GEVCU-ESP32-Adapter (saved by Fritzing 0.9.3b)
circuit board: 8.46667cm x 5.64444cm
breadboards: 1

parts:
  U1 = ESP32-38PinWide [part_number=ESP32-38PinWide]
  J1 = shrouded pin header, 12 pins [form="♂ (shrouded male)"]

nets:
  N1: U1.3.3, J1.pin1
  N2: U1.GPIO35, J1.pin8
  N3: U1.GPIO32, J1.pin7
  N4: U1.GPIO33, J1.pin6
  N5: U1.GND, J1.pin12
  N6: U1.GPIO16, J1.pin2
  N7: U1.GPIO17, J1.pin11

notes:
  Pin 10 - D18
  Pin 3 - TX
  Pin 4 - RX
  Pin 2 - GND
  Pin 1 - 3.3V
  Pin 11 - D42
  Pin 12 - LED

custom parts:
  ESP32-38PinWide: Generic 38-Pin ESP32 with wide format (only access to one side of pins on a breadboard) based on Stephen Lilley's HiLetgo ESP-WROOM-32 ESP32 ESP-32S Development Board.
